# Fritzing sketch rgb kette (saved by Fritzing 0.9.3b)
breadboards: 1

parts:
  Bauteil1 = Arduino Uno (Rev3)
  VCC1 = Battery
  R1 = Resistor [tolerance=±5% resistance=220 package=THT]
  R2 = Resistor [tolerance=±5% resistance=220 package=THT]
  R3 = Resistor [tolerance=±5% resistance=220 package=THT]
  LED1 = RGB LED (com. cathode, rgb) [package="5 mm [THT]"]
  R4 = Resistor [tolerance=±5% resistance=220 package=THT]
  R5 = Resistor [tolerance=±5% resistance=220 package=THT]
  R6 = Resistor [tolerance=±5% resistance=220 package=THT]
  LED2 = RGB LED (com. cathode, rgb) [package="5 mm [THT]"]
  R7 = Resistor [tolerance=±5% resistance=220 package=THT]
  R8 = Resistor [tolerance=±5% resistance=220 package=THT]
  R9 = Resistor [tolerance=±5% resistance=220 package=THT]
  LED3 = RGB LED (com. cathode, rgb) [package="5 mm [THT]"]
  Q1 = NPN-Transistor [package="TO92 [THT]"]
  Q2 = NPN-Transistor [package="TO92 [THT]"]
  Q3 = NPN-Transistor [package="TO92 [THT]"]

nets:
  N1: Bauteil1.D9_PWM, Q3.B
  N2: Bauteil1.D10_PWM/SS, Q2.B
  N3: Bauteil1.D11_PWM/MOSI, Q1.B
  N4: VCC1.-, LED1.common_cathode, LED2.common_cathode, LED3.common_cathode
  N5: VCC1.+, Q1.C, Q2.C, Q3.C
  N6: R1.Pin_0, R5.Pin_0, R7.Pin_0, Q1.E
  N7: R1.Pin_1, LED1.red_anode
  N8: R2.Pin_0, R4.Pin_0, R8.Pin_0, Q2.E
  N9: R2.Pin_1, LED1.green_anode
  N10: R3.Pin_0, R6.Pin_0, R9.Pin_0, Q3.E
  N11: R3.Pin_1, LED1.blue_anode
  N12: R4.Pin_1, LED2.green_anode
  N13: R5.Pin_1, LED2.red_anode
  N14: R6.Pin_1, LED2.blue_anode
  N15: R7.Pin_1, LED3.red_anode
  N16: R8.Pin_1, LED3.green_anode
  N17: R9.Pin_1, LED3.blue_anode

// code stored in the sketch: rgbKette.ino
int bluePin;
int greenPin;
int redPin;

void setup() {
	bluePin = 9;
	greenPin = 10;
	redPin = 11;

	pinMode(bluePin, OUTPUT);
	pinMode(greenPin, OUTPUT);
	pinMode(redPin, OUTPUT);
}

void loop() {
  analogWrite(bluePin, 128);
  analogWrite(greenPin, 128);
  analogWrite(redPin, 128);
}
